# Fritzing sketch ControlledFan (saved by Fritzing 0.9.3b)
breadboards: 3

parts:
  U1 = PIC16F874A/877A [package=dil40]
  LCD1 = LCD screen
  Mod1 = KY-019 5V Relay Module [package="Breakout board"]
  F1 = Fan - Ventilador [package=THT]
  R1 = Resistor [tolerance=±5% resistance=330 package="2512 [SMD]"]
  Y1 = CRYSTAL [package=hc49us]
  T1 = LM35 Temperature Sensor [package="TO92 [THT]"]
  U2 = LM358 [package=dip08]
  U3 = POT [package=pot_alpha_rv16af-20]
  VCC1 = Battery block 9V

nets:
  N1: U1.MCLR, R1.Pin_1
  VDD: U1.VDD, LCD1.VDD, Mod1.+, Mod1.Common, R1.Pin_0, T1.+Vs, U2.G$1_V+, U3.A, VCC1.+
  VSS: U1.VSS, LCD1.VSS, LCD1.V0, LCD1.R/W, Mod1.-, F1.GND, T1.GND, U2.G$1_V-, U3.E, VCC1.-
  N2: U1.OSC1/CLKI, Y1.2
  N3: U1.OSC2/CLKO, Y1.1
  N4: U1.RC0/T1OSO/T1CKI, LCD1.DB4
  N5: U1.RC1/T1OSI/CCP2, LCD1.DB5
  N6: U1.RC2/CCP1, LCD1.DB6
  N7: U1.RC3/SCK/SCL, LCD1.DB7
  N8: U1.RD0/PSP0, Mod1.S
  N9: U1.RC4/SDI/SDA, LCD1.RS
  N10: U1.RC5/SDO, LCD1.E
  N11: T1.Vout, U2.G$1_+IN
  N12: U2.G$1_-IN, U3.S

custom parts:
  PIC16F874A/877A: Microchip 6-bit
  KY-019 5V Relay Module: KY-019 5V Relay module, used to control AC circuits. (Special thanks to vanepp for fixing the PCB holes and other errors)
  Fan - Ventilador: Ventilador de 2 pines, se encuentra comunmente en computadoras de escritorio
